# Fritzing sketch weather_project_esp32 (saved by Fritzing 0.9.3b)
circuit board: 8.54283cm x 5.4498cm
breadboards: 1

parts:
  BME280 = BME280 Breakout
  U1 = ESP32S-HiLetgo [part_number=ESP32S-HiLetgo]
  R1 = Resistor [tolerance=±5% resistance=4.7k package="2010 [SMD]"]
  R2 = Resistor [tolerance=±5% resistance=4.7k package="2010 [SMD]"]
  C2 = Ceramic Capacitor [capacitance=0.1µF package="1206 [SMD, multilayer]"]
  GT1167 = Logic Level Converter
  C1 = Ceramic Capacitor [capacitance=0.1µF package="1206 [SMD, multilayer]"]
  H1 = Hall Sensor [part_number=A3144 package=TO92]
  H2 = Hall Sensor [part_number=A3144 package=TO92]
  AS5600 = AS5600 module
  R4 = Resistor [tolerance=±5% resistance=10k package=THT]
  R3 = Resistor [tolerance=±5% resistance=10k package=THT]
  MH-Real-Time_Clock_Module_3 = RTC_DS1302_module
  S1 = Pushbutton [package="[THT]"]
  R5 = Resistor [tolerance=±5% resistance=10k package=THT]

nets:
  3.3V: BME280.3.3V, U1.3.3, R1.Pin_0, R2.Pin_0, C2.1, GT1167.LV, C1.1, AS5600.Pin_1, MH-Real-Time_Clock_Module_3.VCC, R5.Pin_0
  N1: BME280.SDI/SDA, U1.GPIO21, R2.Pin_1, AS5600.Pin_5
  N2: BME280.SCK/SCL, U1.GPIO22, R1.Pin_1, AS5600.Pin_6
  GND: BME280.GND, U1.GND, C2.0, GT1167.GND, C1.0, H1.GND, H2.GND, AS5600.Pin_3, AS5600.Pin_7, MH-Real-Time_Clock_Module_3.GND, S1.Pin_1, S1.Pin_2
  N3: U1.GPIO25, MH-Real-Time_Clock_Module_3.RST
  N4: U1.GPIO26, MH-Real-Time_Clock_Module_3.DAT
  N5: U1.GPIO27, MH-Real-Time_Clock_Module_3.CLK
  N6: U1.GPIO14, GT1167.RX2_LV
  N7: U1.GPIO12, GT1167.RX_LV
  N8: U1.GPIO0, S1.Pin_3, S1.Pin_4, R5.Pin_1
  N9: GT1167.RX_HV, H1.OUT, R4.Pin_1
  VCC: GT1167.HV, H1.VCC, H2.VCC, R4.Pin_0, R3.Pin_0
  N10: GT1167.RX2_HV, H2.OUT, R3.Pin_1

custom parts:
  ESP32S-HiLetgo: HiLetgo ESP-WROOM-32 ESP32 ESP-32S Development Board 2.4GHz Dual-Mode WiFi + Bluetooth Dual Cores Microcontroller The ESP32 integrated with Antenna switches, RF Balun, power amplifiers, low-noise amplifiers, filters, and management modules, and the entire solution occupies the least area of PCB. 2.4 GHz Wi-Fi plus Bluetooth dual-mode chip, with TSMC Ultra-low power consumption 40nm technology,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
  Hall Sensor: A Hall Sensor
  AS5600 module: .This module is mainly placed behind the stepper motor to obtain the rotation angle of the stepper motor.
  RTC_DS1302_module: Arduino module DS1302 SPI Real Time Clock
